// Logisim project Macchina Caffe.circ as structural Verilog: 1 circuit, main circuit main
module main (
);

  wire _1, _2, _3, _4, A, and_1_out, and_2_out, and_3_out, and_4_out, and_5_out, and_6_out, and_7_out,
       and_8_out, C, C1, C2, C3, C4, CAPPU, CLK, E1, E2, E3, E4, L, LATTE, main_1_out_6, main_1_out_7,
       main_1_out_8, main_1_out_9, main_1_out_10, main_1_out_11, main_1_out_12, main_1_out_13, main_22_out_9,
       N, OFF_out, ON_out, or_1_out, or_2_out, or_3_out, or_4_out, or_5_out, or_6_out, P1, P2, P3, P4, R1,
       R2, R3, R4, R5, R6, R7, R8, R9, R10, R11, R12, SCHIUMA, TEMPERATURA;
  wire [4:0] main_5_out_7, main_5_out_8, main_5_out_9, main_5_out_10, main_5_out_11, main_11_out_7,
       main_11_out_8, main_11_out_9, main_11_out_10, main_11_out_11, main_16_out_7, main_16_out_8,
       main_16_out_9, main_16_out_10, main_16_out_11, main_18_out_7, main_18_out_8, main_18_out_9,
       main_18_out_10, main_18_out_11, main_22_out_4, main_22_out_5, main_22_out_6, main_22_out_7,
       main_22_out_8, main_23_out_4, main_23_out_5, main_23_out_6, main_23_out_7, main_23_out_8;

  and and_1 (and_1_out, A, SCHIUMA);
  Button OFF (.out(OFF_out));
  Button ON (.out(ON_out));
  Clock clock_1 (.out(CLK));
  Accensione_Spegnimento_main main_1 (
    .CLK(CLK), .ACCENSIONE(ON_out), .SPEGNIMENTO(OFF_out), .Alza_temperatura(and_1_out),
    .Reset_temperatura(TEMPERATURA), .SEGNALE_ON(A), .out_6(main_1_out_6), .out_7(main_1_out_7),
    .out_8(main_1_out_8), .out_9(main_1_out_9), .out_10(main_1_out_10), .out_11(main_1_out_11),
    .out_12(main_1_out_12), .out_13(main_1_out_13));
  DotMatrix #(.inputtype("row"), .matrixcols(1), .matrixrows(1)) dotmatrix_1 (.row0(main_1_out_6));
  DotMatrix #(.inputtype("row"), .matrixcols(1), .matrixrows(1)) dotmatrix_2 (.row0(main_1_out_7));
  DotMatrix #(.inputtype("row"), .matrixcols(1), .matrixrows(1)) dotmatrix_3 (.row0(main_1_out_8));
  DotMatrix #(.inputtype("row"), .matrixcols(1), .matrixrows(1)) dotmatrix_4 (.row0(main_1_out_9));
  DotMatrix #(.inputtype("row"), .matrixcols(1), .matrixrows(1)) dotmatrix_5 (.row0(main_1_out_10));
  DotMatrix #(.inputtype("row"), .matrixcols(1), .matrixrows(1)) dotmatrix_6 (.row0(main_1_out_11));
  DotMatrix #(.inputtype("row"), .matrixcols(1), .matrixrows(1)) dotmatrix_7 (.row0(main_1_out_12));
  DotMatrix #(.inputtype("row"), .matrixcols(1), .matrixrows(1)) dotmatrix_8 (.row0(main_1_out_13));
  Button \Caffè_lungo  (.out(L));
  Button \Caffè_corto  (.out(C));
  Button \Caffè  (.out(N));
  Selezione_canale_main main_2 (.in_1(L), .in_2(C1), .in_3(A), .out_4(R1));
  Selezione_canale_main main_3 (.in_1(C), .in_2(C1), .in_3(A), .out_4(R5));
  Selezione_canale_main main_4 (.in_1(N), .in_2(C1), .in_3(A), .out_4(R9));
  Button u__1 (.out(_1));
  or or_1 (or_1_out, R1, R9, R5);
  and and_2 (and_2_out, CAPPU, C1);
  DotMatrix #(.inputtype("row"), .matrixrows(1)) dotmatrix_9 (.row0(main_5_out_7));
  Riempimento_tazza_main main_5 (
    .\Caffè_lungo (R1), .\Caffè_corto (R5), .\Caffè (R9), .CLK(CLK), .Reset(E1), .Schiuma(and_2_out),
    .out_7(main_5_out_7), .out_8(main_5_out_8), .out_9(main_5_out_9), .out_10(main_5_out_10),
    .out_11(main_5_out_11), .Tazza_piena(P1));
  DotMatrix #(.inputtype("row"), .matrixrows(4)) dotmatrix_10 (
    .row0(main_5_out_8), .row1(main_5_out_9), .row2(main_5_out_10), .row3(main_5_out_11));
  Button _1_2 (.out(E1));
  Bottone_premuto_1bit_main main_6 (.CLK(CLK), .D(_1), .R(or_1_out), .out_4(C1));
  Selezione_canale_main main_7 (.in_1(L), .in_2(C2), .in_3(A), .out_4(R2));
  Selezione_canale_main main_8 (.in_1(C), .in_2(C2), .in_3(A), .out_4(R6));
  Selezione_canale_main main_9 (.in_1(N), .in_2(C2), .in_3(A), .out_4(R10));
  Button u__2 (.out(_2));
  Bottone_premuto_1bit_main main_10 (.CLK(CLK), .D(_2), .R(or_2_out), .out_4(C2));
  or or_2 (or_2_out, R2, R10, R6);
  and and_3 (and_3_out, CAPPU, C2);
  Riempimento_tazza_main main_11 (
    .\Caffè_lungo (R2), .\Caffè_corto (R6), .\Caffè (R10), .CLK(CLK), .Reset(E2), .Schiuma(and_3_out),
    .out_7(main_11_out_7), .out_8(main_11_out_8), .out_9(main_11_out_9), .out_10(main_11_out_10),
    .out_11(main_11_out_11), .Tazza_piena(P2));
  DotMatrix #(.inputtype("row"), .matrixrows(1)) dotmatrix_11 (.row0(main_11_out_7));
  DotMatrix #(.inputtype("row"), .matrixrows(4)) dotmatrix_12 (
    .row0(main_11_out_8), .row1(main_11_out_9), .row2(main_11_out_10), .row3(main_11_out_11));
  Button _2_2 (.out(E2));
  and and_4 (and_4_out, CAPPU, C3);
  Selezione_canale_main main_12 (.in_1(L), .in_2(C3), .in_3(A), .out_4(R3));
  Selezione_canale_main main_13 (.in_1(C), .in_2(C3), .in_3(A), .out_4(R7));
  Selezione_canale_main main_14 (.in_1(N), .in_2(C3), .in_3(A), .out_4(R11));
  Button u__3 (.out(_3));
  Bottone_premuto_1bit_main main_15 (.CLK(CLK), .D(_3), .R(or_3_out), .out_4(C3));
  or or_3 (or_3_out, R3, R11, R7);
  DotMatrix #(.inputtype("row"), .matrixrows(1)) dotmatrix_13 (.row0(main_16_out_7));
  Riempimento_tazza_main main_16 (
    .\Caffè_lungo (R3), .\Caffè_corto (R7), .\Caffè (R11), .CLK(CLK), .Reset(E3), .Schiuma(and_4_out),
    .out_7(main_16_out_7), .out_8(main_16_out_8), .out_9(main_16_out_9), .out_10(main_16_out_10),
    .out_11(main_16_out_11), .Tazza_piena(P3));
  DotMatrix #(.inputtype("row"), .matrixrows(4)) dotmatrix_14 (
    .row0(main_16_out_8), .row1(main_16_out_9), .row2(main_16_out_10), .row3(main_16_out_11));
  Selezione_canale_main main_17 (.in_1(L), .in_2(C4), .in_3(A), .out_4(R4));
  Button _3_2 (.out(E3));
  and and_5 (and_5_out, CAPPU, C4);
  Riempimento_tazza_main main_18 (
    .\Caffè_lungo (R4), .\Caffè_corto (R8), .\Caffè (R12), .CLK(CLK), .Reset(E4), .Schiuma(and_5_out),
    .out_7(main_18_out_7), .out_8(main_18_out_8), .out_9(main_18_out_9), .out_10(main_18_out_10),
    .out_11(main_18_out_11), .Tazza_piena(P4));
  DotMatrix #(.inputtype("row"), .matrixrows(1)) dotmatrix_15 (.row0(main_18_out_7));
  DotMatrix #(.inputtype("row"), .matrixrows(4)) dotmatrix_16 (
    .row0(main_18_out_8), .row1(main_18_out_9), .row2(main_18_out_10), .row3(main_18_out_11));
  Selezione_canale_main main_19 (.in_1(C), .in_2(C4), .in_3(A), .out_4(R8));
  Selezione_canale_main main_20 (.in_1(N), .in_2(C4), .in_3(A), .out_4(R12));
  Button u__4 (.out(_4));
  Bottone_premuto_1bit_main main_21 (.CLK(CLK), .D(_4), .R(or_4_out), .out_4(C4));
  or or_4 (or_4_out, R4, R12, R8);
  Button _4_2 (.out(E4));
  and and_6 (and_6_out, SCHIUMA, A);
  Riempi_latte_main main_22 (
    .Latte(LATTE), .CLK(CLK), .Reset(and_6_out), .out_4(main_22_out_4), .out_5(main_22_out_5),
    .out_6(main_22_out_6), .out_7(main_22_out_7), .out_8(main_22_out_8), .out_9(main_22_out_9));
  DotMatrix #(.inputtype("row"), .matrixrows(5)) dotmatrix_17 (
    .row0(main_22_out_4), .row1(main_22_out_5), .row2(main_22_out_6), .row3(main_22_out_7),
    .row4(main_22_out_8));
  or or_5 (or_5_out, C1, C2, C3, C4);
  Button Carica_latte (.out(LATTE));
  Button Fai_schiuma (.out(SCHIUMA));
  Button Cappuccino (.out(CAPPU));
  or or_6 (or_6_out, P1, P2, P3, P4);
  and and_7 (and_7_out, or_5_out, or_6_out, CAPPU);
  Riempi_latte_main main_23 (
    .Latte(and_8_out), .CLK(CLK), .Reset(and_7_out), .out_4(main_23_out_4), .out_5(main_23_out_5),
    .out_6(main_23_out_6), .out_7(main_23_out_7), .out_8(main_23_out_8), .out_9(TEMPERATURA));
  DotMatrix #(.inputtype("row"), .matrixrows(5)) dotmatrix_18 (
    .row0(main_23_out_4), .row1(main_23_out_5), .row2(main_23_out_6), .row3(main_23_out_7),
    .row4(main_23_out_8));
  and and_8 (and_8_out, main_22_out_9, A, SCHIUMA);

  // Notes on the sheet:
  //   Temperatura acqua
  //   Selezione bevanda
  //   Alta
  //   Bassa
  //   Selezione canale caffè
  //   Preleva tazza
  //   Prepara schiuma per cappuccini
endmodule
