// Logisim project Riempi_latte.circ as structural Verilog: 1 circuit, main circuit main
module main (
  input  Reset,
  input  Latte,
  input  CLK,
  output [4:0] out_4,
  output [4:0] out_5,
  output [4:0] out_6,
  output [4:0] out_7,
  output [4:0] out_8,
  output out_9
);

  wire shift_register_1_out, shift_register_2_p3, shift_register_3_p3;
  wire [4:0] main_1_out_4, undriven;

  Bottone_premuto_main main_1 (.CLK(CLK), .D(Latte), .R(Reset), .out_4(main_1_out_4));
  Shift_Register #(.length(2), .parallel("false")) shift_register_1 (
    .in(Reset), .clk(CLK), .out(shift_register_1_out));  // open: shift, load, clr, d0, q0, d1, q1
  // Shift_Register #(.length(3), .parallel("false")) shift_register_2: pin names not known; wires that end beside it: shift_register_1_out, CLK, shift_register_2_p3
  // Shift_Register #(.length(4), .parallel("false")) shift_register_3: pin names not known; wires that end beside it: shift_register_2_p3, CLK, shift_register_3_p3, shift_register_2_p3
  // Shift_Register #(.width(5), .length(5), .parallel("false")) shift_register_4: pin names not known; wires that end beside it: out_6, CLK, Reset, out_5
  // Shift_Register #(.width(5), .length(5), .parallel("false")) shift_register_5: pin names not known; wires that end beside it: out_7, CLK, shift_register_1_out, out_6
  // Shift_Register #(.width(5), .length(5), .parallel("false")) shift_register_6: pin names not known; wires that end beside it: out_8, CLK, shift_register_2_p3, out_7
  // Shift_Register #(.width(5), .length(5), .parallel("false")) shift_register_7: pin names not known; wires that end beside it: main_1_out_4, CLK, shift_register_3_p3, out_8
  Shift_Register #(.width(5), .length(10), .parallel("false")) shift_register_8 (
    .in(out_5), .clk(CLK));  // open: shift, out, load, clr, d0, q0, d1, q1, d2, q2, d3, q3, d4, q4, d5, q5, d6, q6, d7, q7, d8, q8, d9, q9
  Bit_Extender #(.in_width(5), .out_width(1), .\type ("sign")) bit_extender_1 (.in(undriven), .out(out_9));

  assign out_4 = {5{1'b0}};
endmodule
