// Logisim project Bottone_premuto.circ as structural Verilog: 1 circuit, main circuit main
module main (
  input  CLK,
  input  D,
  input  R,
  output [4:0] out_4
);

  wire and_1_out, d_ff_1_q, or_1_out;

  or or_1 (or_1_out, d_ff_1_q, D);
  and and_1 (and_1_out, or_1_out, ~R);  // AND_Gate
  D_Flip_Flop d_ff_1 (.clk(CLK), .D(and_1_out), .Q(d_ff_1_q));  // open: Qn, preset, en, reset
  assign out_4 = {{4{d_ff_1_q}}, d_ff_1_q};  // Bit_Extender bit_extender_1
endmodule
