// Logisim project Bottone_premuto_1bit.circ as structural Verilog: 1 circuit, main circuit main
module main (
  input  CLK,
  input  D,
  input  R,
  output out_4
);

  wire and_1_out, or_1_out;

  or or_1 (or_1_out, out_4, D);
  and and_1 (and_1_out, or_1_out, ~R);  // AND_Gate
  D_Flip_Flop d_ff_1 (.clk(CLK), .D(and_1_out), .Q(out_4));  // open: Qn, preset, en, reset
endmodule
