// Logisim project Riempimento_tazza.circ as structural Verilog: 1 circuit, main circuit main
module main (
  input  Reset,
  input  Schiuma,
  input  \Caffè_lungo ,
  input  \Caffè_corto ,
  input  \Caffè ,
  input  CLK,
  output [4:0] out_7,
  output [4:0] out_8,
  output [4:0] out_9,
  output [4:0] out_10,
  output [4:0] out_11,
  output Tazza_piena
);

  wire [4:0] and_1_out, and_2_out, main_1_out_4, main_2_out_4, main_3_out_4, main_4_out_4, or_1_out, or_2_out;

  Bottone_premuto_main main_1 (.CLK(CLK), .D(\Caffè_lungo ), .R(Reset), .out_4(main_1_out_4));
  Bottone_premuto_main main_2 (.CLK(CLK), .D(\Caffè_corto ), .R(Reset), .out_4(main_2_out_4));
  Bottone_premuto_main main_3 (.CLK(CLK), .D(\Caffè ), .R(Reset), .out_4(main_3_out_4));
  assign or_1_out = main_3_out_4 | main_2_out_4 | main_1_out_4;  // OR_Gate or_1, 5 bits wide
  assign and_1_out = main_1_out_4 & out_9;  // AND_Gate and_1, 5 bits wide
  assign and_2_out = or_2_out & out_10;  // AND_Gate and_2, 5 bits wide
  assign or_2_out = main_1_out_4 | main_3_out_4;  // OR_Gate or_2, 5 bits wide
  // Shift_Register #(.width(5), .length(5), .parallel("false")) shift_register_1: pin names not known; wires that end beside it: and_1_out, CLK, Reset, out_8
  // Shift_Register #(.width(5), .length(5), .parallel("false")) shift_register_2: pin names not known; wires that end beside it: and_2_out, CLK, Reset, out_9
  // Shift_Register #(.width(5), .length(5), .parallel("false")) shift_register_3: pin names not known; wires that end beside it: out_11, CLK, Reset, out_10
  // Shift_Register #(.width(5), .length(5), .parallel("false")) shift_register_4: pin names not known; wires that end beside it: or_1_out, CLK, Reset, out_11
  Bottone_premuto_main main_4 (.CLK(CLK), .D(Schiuma), .R(Reset), .out_4(main_4_out_4));
  assign out_7 = out_8 & main_4_out_4;  // AND_Gate and_3, 5 bits wide
  Bit_Extender #(.in_width(5), .out_width(1), .\type ("sign")) bit_extender_1 (.in(out_8), .out(Tazza_piena));
endmodule
